# Fritzing sketch wemos-alarm (saved by Fritzing 0.9.3b)

parts:
  WeMos_D1_Mini1 = WeMos D1 Mini
  SIM800L_BO1 = SIM800L BO
  M1 = RioRand LM2596
  R3 = Resistor [tolerance=±5% resistance=2.2k package=THT]
  R4 = Resistor [tolerance=±5% resistance=10k package=THT]

nets:
  N1: WeMos_D1_Mini1.D1, R3.Pin_0
  N2: WeMos_D1_Mini1.D2, SIM800L_BO1.pin_5
  N3: WeMos_D1_Mini1.G, SIM800L_BO1.pin_6, M1.Pin_4, R4.Pin_1
  N4: SIM800L_BO1.PIN2, M1.Pin_3
  N5: SIM800L_BO1.pin_4, R3.Pin_1, R4.Pin_0

notes:
  Как работает reset?
  Напряжение SIM800L 3.5-4.4V; 2A (ср. 4V)
  Уровень логики SIM800L 2.1-3.1 V (ср. 2.6V)
  Уровень логики Wemos 3.3 V
